// Logisim project Teste nands.circ as structural Verilog: 1 circuit, main circuit main
module main (
  input  D,
  input  En
);

  wire and_1_out, and_2_out, button_1_out, d_ff_1_q, nand_1_out, nand_2_out, nand_3_out, not_1_out, or_1_out,
       undriven;

  not not_1 (not_1_out, En);
  and and_1 (and_1_out, not_1_out, D);
  or or_1 (or_1_out, and_1_out, and_2_out);
  and and_2 (and_2_out, ~not_1_out, d_ff_1_q);  // AND_Gate
  LED led_1 (.in(or_1_out));
  Button button_1 (.out(button_1_out));
  D_Flip_Flop d_ff_1 (.clk(button_1_out), .D(D), .Q(d_ff_1_q), .en(undriven));  // open: Qn, preset, reset
  nand nand_1 (nand_1_out, En, D);
  nand nand_2 (nand_2_out, not_1_out, d_ff_1_q);
  nand nand_3 (nand_3_out, nand_1_out, nand_2_out);
  LED led_2 (.in(nand_3_out));
endmodule
